# Fritzing sketch link-pedal2key (saved by Fritzing 0.9.3b)

parts:
  パーツ1 = Arduino Micro (Rev3)
  パーツ2 = Thumb Joystick
  U1 = 2.5mm Audio Jack [package=stereojack2.5mm_stereojack2.5mm]

nets:
  GND: パーツ1.GND, パーツ2.GND, U1.RIGHT
  N1: パーツ1.D2/SDA, パーツ2.VCC
  N2: パーツ1.D7, U1.LEFT
  N3: パーツ1.5V, パーツ2.SEL
  N4: パーツ1.A1, パーツ2.VERT
  N5: パーツ1.A0, パーツ2.HORZ
